// Logisim project SystemSide_Draft.circ as structural Verilog: 1 circuit, main circuit main
module main (
  input  [1:0] in_1,
  input  [7:0] data__8b,
  input  [3:0] Address,
  input  R_W,
  input  in_5
);

  wire _0_out, _1_out, _2_out, _3_out, _4_out, _5_out, _6_out, _7_out, _8_out, _9_out, clock_1_out,
       main_1_out_2, main_1_out_3, main_1_out_4, main_1_out_5, main_1_out_6, main_1_out_7, main_1_out_8,
       main_1_out_9, main_1_out_10, main_1_out_11, main_1_out_12, main_1_out_13, main_1_out_14,
       main_1_out_15, main_1_out_16, main_1_out_17, main_1_out_18, main_1_out_19, main_1_out_20,
       main_1_out_21, main_1_out_22;
  wire [7:0] keypadblackbox_1_out_11, multiplexer_2_out, ram_1_p6, ram_1_p15;

  _7_Segment_Display u_7_segment_display_1 (
    .g(main_1_out_17), .f(main_1_out_18), .a(main_1_out_2), .b(main_1_out_5), .e(main_1_out_14),
    .d(main_1_out_11), .c(main_1_out_8));  // open: dp
  Clock clock_1 (.out(clock_1_out));
  Button _1 (.out(_1_out));
  Button _4 (.out(_4_out));
  Button _7 (.out(_7_out));
  _7_Segment_Display u_7_segment_display_2 (
    .g(main_1_out_19), .f(main_1_out_20), .a(main_1_out_3), .b(main_1_out_6), .e(main_1_out_15),
    .d(main_1_out_12), .c(main_1_out_9));  // open: dp
  // RAM ram_1: pin names not known; wires that end beside it: R_W, Address[0], Address[1], Address[2], Address[3], ram_1_p6[0], ram_1_p6[1], ram_1_p6[2], ram_1_p6[3], ram_1_p6[4], ram_1_p6[5], ram_1_p6[6], ram_1_p6[7], clock_1_out, ram_1_p15[0], ram_1_p15[1], ram_1_p15[2], ram_1_p15[3], ram_1_p15[4], ram_1_p15[5], ram_1_p15[6], ram_1_p15[7]
  Button _2 (.out(_2_out));
  Button _5 (.out(_5_out));
  Button _8 (.out(_8_out));
  Button _0 (.out(_0_out));
  Button _3 (.out(_3_out));
  Button _6 (.out(_6_out));
  Button _9 (.out(_9_out));
  keypadblackbox keypadblackbox_1 (
    .in_1(_0_out), .in_2(_1_out), .in_3(_2_out), .in_4(_3_out), .in_5(_4_out), .in_6(_5_out), .in_7(_6_out),
    .in_8(_7_out), .in_9(_8_out), .in_10(_9_out), .out_11(keypadblackbox_1_out_11));
  _7_Segment_Display u_7_segment_display_3 (
    .g(main_1_out_21), .f(main_1_out_22), .a(main_1_out_4), .b(main_1_out_7), .e(main_1_out_16),
    .d(main_1_out_13), .c(main_1_out_10));  // open: dp
  Multiplexer #(.width(8), .enable("false")) multiplexer_1 (
    .in0(multiplexer_2_out), .in1(keypadblackbox_1_out_11), .out(ram_1_p6), .sel(in_5));
  Multiplexer #(.select(2), .width(8), .enable("false")) multiplexer_2 (
    .in0(ram_1_p15), .in1(data__8b), .in2(keypadblackbox_1_out_11), .out(multiplexer_2_out), .sel(in_1));  // open: in3
  _8bitTo3dec_main main_1 (
    .out_19(main_1_out_19), .out_20(main_1_out_20), .out_15(main_1_out_15), .out_9(main_1_out_9),
    .out_12(main_1_out_12), .out_6(main_1_out_6), .out_3(main_1_out_3), .out_4(main_1_out_4),
    .out_7(main_1_out_7), .out_10(main_1_out_10), .out_13(main_1_out_13), .out_16(main_1_out_16),
    .out_21(main_1_out_21), .out_22(main_1_out_22), .out_2(main_1_out_2), .out_5(main_1_out_5),
    .out_8(main_1_out_8), .out_11(main_1_out_11), .out_14(main_1_out_14), .out_17(main_1_out_17),
    .out_18(main_1_out_18), .in_1(multiplexer_2_out));

  // Notes on the sheet:
  //   RAM/KeYPAD/MBR to BUS
  //   MBR/KEYPAD to Ram
endmodule
